// Logisim project mapa2.circ as structural Verilog: 11 circuits, main circuit main
module main (
  input  [3:0] \input 
);

  wire clock_1_out, LogicaEstados_ja, LogicaEstados_jb, LogicaEstados_jc, LogicaEstados_jd, LogicaEstados_ka,
       LogicaEstados_kb, LogicaEstados_kc, LogicaEstados_kd, LogicaSalida_a, LogicaSalida_b, LogicaSalida_c,
       LogicaSalida_d, LogicaSalida_e, LogicaSalida_f, LogicaSalida_g;
  wire [3:0] FFJK_salida;

  Clock clock_1 (.out(clock_1_out));
  LogicaEstados LogicaEstados (
    .estado(FFJK_salida), .Ja(LogicaEstados_ja), .Ka(LogicaEstados_ka), .Jb(LogicaEstados_jb),
    .Kb(LogicaEstados_kb), .Jc(LogicaEstados_jc), .Kc(LogicaEstados_kc), .Jd(LogicaEstados_jd),
    .Kd(LogicaEstados_kd));
  FFJK FFJK (
    .Jd(LogicaEstados_jd), .Kd(LogicaEstados_kd), .Jc(LogicaEstados_jc), .Kc(LogicaEstados_kc),
    .Kb(LogicaEstados_kb), .Jb(LogicaEstados_jb), .Ka(LogicaEstados_ka), .Ja(LogicaEstados_ja),
    .salida(FFJK_salida), .reloj(clock_1_out), .\input (\input ));
  LogicaSalida LogicaSalida (
    .in_1(FFJK_salida), .a(LogicaSalida_a), .b(LogicaSalida_b), .c(LogicaSalida_c), .d(LogicaSalida_d),
    .e(LogicaSalida_e), .f(LogicaSalida_f), .g(LogicaSalida_g));
  _7_Segment_Display u_7_segment_display_1 (
    .g(LogicaSalida_g), .f(LogicaSalida_f), .a(LogicaSalida_a), .b(LogicaSalida_b), .e(LogicaSalida_e),
    .d(LogicaSalida_d), .c(LogicaSalida_c));  // open: dp
endmodule

module FFJK (
  input  reloj,
  input  Ja,
  input  Ka,
  input  Jb,
  input  [3:0] \input ,
  input  Kb,
  input  Jc,
  input  Kc,
  input  Jd,
  input  Kd,
  output [3:0] salida
);

  wire d_ff_1_q;
  wire [3:0] D_q;

  J_K_Flip_Flop A (.J(Ja), .clk(reloj), .K(Ka), .Q(D_q[3]));  // open: Qn, preset, en, reset
  J_K_Flip_Flop B (.J(Jb), .clk(reloj), .K(Kb), .Q(D_q[2]));  // open: Qn, preset, en, reset
  J_K_Flip_Flop C (.J(Jc), .clk(reloj), .K(Kc), .Q(D_q[1]));  // open: Qn, preset, en, reset
  J_K_Flip_Flop D (.J(Jd), .clk(reloj), .K(Kd), .Q(D_q[0]));  // open: Qn, preset, en, reset
  Multiplexer #(.width(4)) multiplexer_1 (.in0(\input ), .in1(D_q), .out(salida), .sel(d_ff_1_q));  // open: en
  D_Flip_Flop d_ff_1 (.clk(reloj), .D(1'b1), .Q(d_ff_1_q));  // open: Qn, preset, en, reset
endmodule

module LogicaSalida (
  input  [3:0] in_1,
  output a,
  output b,
  output c,
  output d,
  output e,
  output f,
  output g
);

  SalidaA u_a (.in_1(in_1), .Sa(a));
  SalidaB u_b (.in_1(in_1), .Sb(b));
  SalidaC u_c (.in_1(in_1), .Sc(c));
  SalidaD u_d (.in_1(in_1), .Sd(d));
  SalidaE u_e (.in_1(in_1), .Se(e));
  SalidaF u_f (.in_1(in_1), .Sf(f));
  SalidaG u_g (.in_1(in_1), .Sg(g));
endmodule

module LogicaEstados (
  input  [3:0] estado,
  output Ja,
  output Ka,
  output Jb,
  output Kb,
  output Jc,
  output Kc,
  output Jd,
  output Kd
);

  wire BC_out, BD_out, CD_2_out, CD_out, minus_A_B_out, minus_AB_out, minus_AC_out, not_1_out, not_2_out,
       not_3_out;

  not not_1 (not_1_out, estado[3]);
  not not_2 (not_2_out, estado[2]);
  not not_3 (not_3_out, estado[1]);
  and BD (BD_out, estado[2], estado[0]);
  and BC (BC_out, estado[2], estado[1]);
  and BCD (Ka, estado[1], estado[2], estado[0]);
  and CD (CD_out, estado[1], estado[0]);
  and minus_AC (minus_AC_out, not_1_out, estado[1]);
  and AD (Jc, estado[0], estado[3]);
  and minus_AB (minus_AB_out, not_1_out, estado[2]);
  and CD_2 (CD_2_out, estado[1], estado[0]);
  and minus_A_B (minus_A_B_out, not_1_out, not_2_out);
  or BD___BC (Ja, BD_out, BC_out);
  or CD____AC (Kb, CD_out, minus_AC_out);
  or minus_AB___CD (Kc, minus_AB_out, CD_2_out);
  or A____A_B____C (Jd, estado[3], minus_A_B_out, not_3_out);
  or A____A_B___C (Kd, estado[3], minus_A_B_out, estado[1]);

  assign Jb = estado[0];
endmodule

module SalidaA (
  input  [3:0] in_1,
  output Sa
);

  wire B_C_out, minus_BCD_out, minus_C_D_out, not_1_out, not_2_out, not_3_out;

  not not_1 (not_1_out, in_1[0]);
  not not_2 (not_2_out, in_1[1]);
  not not_3 (not_3_out, in_1[2]);
  and minus_C_D (minus_C_D_out, not_1_out, not_2_out);
  and B_C (B_C_out, not_2_out, in_1[2]);
  and minus_BCD (minus_BCD_out, not_3_out, in_1[1], in_1[0]);
  or or_1 (Sa, minus_C_D_out, B_C_out, minus_BCD_out, in_1[3]);
endmodule

module SalidaB (
  input  [3:0] in_1,
  output Sb
);

  wire AB_out, AD_out, BD_out, C_D_out, minus_A_B_C_out, not_1_out, not_2_out, not_3_out, not_4_out;

  not not_1 (not_1_out, in_1[1]);
  not not_2 (not_2_out, in_1[2]);
  not not_3 (not_3_out, in_1[3]);
  not not_4 (not_4_out, in_1[0]);
  and minus_A_B_C (minus_A_B_C_out, not_1_out, not_2_out, not_3_out);
  and BD (BD_out, in_1[0], in_1[2]);
  and AD (AD_out, in_1[3], in_1[0]);
  and AB (AB_out, in_1[3], in_1[2]);
  and C_D (C_D_out, in_1[1], not_4_out);
  or or_1 (Sb, minus_A_B_C_out, BD_out, AD_out, AB_out, C_D_out);
endmodule

module SalidaC (
  input  [3:0] in_1,
  output Sc
);

  or or_1 (Sc, in_1[0], in_1[1], in_1[2], in_1[3]);
endmodule

module SalidaD (
  input  [3:0] in_1,
  output Sd
);

  wire A_B_C_out, AC_D_out, minus_A_BCD_out, minus_A_C_D_out, not_1_out, not_2_out, not_3_out, not_4_out;

  not not_1 (not_1_out, in_1[0]);
  not not_2 (not_2_out, in_1[1]);
  not not_3 (not_3_out, in_1[3]);
  not not_4 (not_4_out, in_1[2]);
  and minus_A_C_D (minus_A_C_D_out, not_1_out, not_2_out, not_3_out);
  and A_B_C (A_B_C_out, in_1[3], not_4_out, not_2_out);
  and minus_A_BCD (minus_A_BCD_out, not_3_out, not_4_out, in_1[1], in_1[0]);
  and AC_D (AC_D_out, in_1[3], in_1[1], not_1_out);
  or or_1 (Sd, minus_A_C_D_out, A_B_C_out, minus_A_BCD_out, AC_D_out);
endmodule

module SalidaE (
  input  [3:0] in_1,
  output Se
);

  wire AC_D_out, minus_B_C_D_out, not_1_out, not_2_out, not_3_out;

  not not_1 (not_1_out, in_1[0]);
  not not_2 (not_2_out, in_1[1]);
  not not_3 (not_3_out, in_1[2]);
  and AC_D (AC_D_out, not_1_out, in_1[1], in_1[3]);
  and minus_B_C_D (minus_B_C_D_out, not_1_out, not_2_out, not_3_out);
  or or_1 (Se, AC_D_out, minus_B_C_D_out);
endmodule

module SalidaF (
  input  [3:0] in_1,
  output Sf
);

  wire A_D_out, B_D_out, BC_out, minus_A_BD_out, not_1_out, not_2_out, not_3_out;

  not not_1 (not_1_out, in_1[2]);
  not not_2 (not_2_out, in_1[3]);
  not not_3 (not_3_out, in_1[0]);
  and minus_A_BD (minus_A_BD_out, in_1[0], not_1_out, not_2_out);
  and B_D (B_D_out, in_1[2], not_3_out);
  and A_D (A_D_out, in_1[3], not_3_out);
  and BC (BC_out, in_1[1], in_1[2]);
  or or_1 (Sf, minus_A_BD_out, B_D_out, A_D_out, BC_out);
endmodule

module SalidaG (
  input  [3:0] in_1,
  output Sg
);

  wire A_D_out, BC_out, minus_A_BD_out, minus_B_C_out, minus_C_D_out, not_1_out, not_2_out, not_3_out,
       not_4_out;

  not not_1 (not_1_out, in_1[2]);
  not not_2 (not_2_out, in_1[3]);
  not not_3 (not_3_out, in_1[0]);
  not not_4 (not_4_out, in_1[1]);
  and minus_A_BD (minus_A_BD_out, in_1[0], not_1_out, not_2_out);
  and A_D (A_D_out, in_1[3], not_3_out);
  and minus_B_C (minus_B_C_out, not_1_out, not_4_out);
  and BC (BC_out, in_1[2], in_1[1]);
  and minus_C_D (minus_C_D_out, not_4_out, not_3_out);
  or or_1 (Sg, minus_A_BD_out, A_D_out, minus_B_C_out, BC_out, minus_C_D_out);
endmodule
